# Fritzing sketch Lcd_I2c8574_ESP32NodeMCU (saved by Fritzing 0.9.10b)

parts:
  LCD2004-I2C1 = LCD2004-I2C
  U2 = ESP32-WROOM-32D-NodeMCU
  U3 = USB+SHIELD [package=usb-b-pth]

nets:
  N1: LCD2004-I2C1.GND, U2.CMD
  N2: LCD2004-I2C1.VCC, U3.VBUS
  N3: LCD2004-I2C1.SDA, U2.G21
  N4: LCD2004-I2C1.SCL, U2.G22

custom parts:
  LCD2004-I2C: A standard character display with 4x20 characters. Comes in many colors with LCM2004 IIC attached.
