# Fritzing sketch Lcd_I2c8574_PyBoard (saved by Fritzing 0.9.10b)

parts:
  LCD2004-I2C1 = LCD2004-I2C
  pyboard1 = Micro Python pyboard [part_number=PYBv10b]

nets:
  N1: LCD2004-I2C1.GND, pyboard1.P9A_GND
  N2: LCD2004-I2C1.VCC, pyboard1.P10A_VIN
  N3: LCD2004-I2C1.SDA, pyboard1.Y10
  N4: LCD2004-I2C1.SCL, pyboard1.Y9

custom parts:
  LCD2004-I2C: A standard character display with 4x20 characters. Comes in many colors with LCM2004 IIC attached.
